# Fritzing sketch cat_laser_sans_pca_v2 (saved by Fritzing 0.9.6b)
circuit board: 8.46667cm x 5.64444cm
breadboards: 1

parts:
  R3 = Resistor [tolerance=±5% power=0.25 resistance=100k package=THT]
  S1 = Pushbutton [package=THT]
  Part1 = Arduino Nano (Rev3.0)
  R4 = Trimmer Potentiometer [maximum_resistance=10kΩ package=THT]
  R5 = Trimmer Potentiometer [maximum_resistance=10kΩ package=THT]
  J1 = Basic Servo
  J2 = Basic Servo
  LED1 = smd LED [color="Red (633nm)" package="0603 [SMD]"]
  LED2 = smd LED [color="Red (633nm)" package="0603 [SMD]"]

nets:
  N1: R3.Pin_0, S1.leg0, Part1.D4
  GND: R3.Pin_1, Part1.GND, R4.leg1, R5.leg1, J1.gnd, J2.gnd, LED1.cathode, LED2.cathode
  VCC: S1.leg1, Part1.5V, R4.leg2, R5.leg2, J1.vcc, J2.vcc
  N2: Part1.D2, LED1.anode
  N3: Part1.D3, LED2.anode
  N4: Part1.D9, J2.pulse
  N5: Part1.D10, J1.pulse
  N6: Part1.A1, R5.wiper
  N7: Part1.A0, R4.wiper
